# Fritzing sketch arduinoESC (saved by Fritzing 0.9.3b)
breadboards: 1

parts:
  PUSHBUTTON = Pushbutton [package="[SMD]"]
  CL_SWITCH = SPST Switch [package=switch-spdt_kit]
  texas_instruments1 = Arduino Uno (Rev3) - ICSP
  10K = 10K Ω Resistor [package="1206 [SMD]"]
  10K_2 = 10K Ω Resistor [package="1206 [SMD]"]
  LM2907 = LM2907M [package=THT]  # not connected
  U1 = POT [package=pot_mammoth]

nets:
  N1: PUSHBUTTON.Pin_1, PUSHBUTTON.Pin_2, texas_instruments1.D4, 10K.Pin_0
  N2: PUSHBUTTON.Pin_3, PUSHBUTTON.Pin_4, CL_SWITCH.S, texas_instruments1.3V3, U1.E
  N3: CL_SWITCH.O, 10K_2.Pin_0
  N4: CL_SWITCH.P, texas_instruments1.D2
  N5: texas_instruments1.A0, U1.S
  N6: 10K.Pin_1, 10K_2.Pin_1, U1.A

notes:
  ElectroTurbine

custom parts:
  10K Ω Resistor: A generic resistor
  LM2907M: Texas Instruments Demodulator
