# Fritzing sketch photonESC (saved by Fritzing 0.9.3b)
breadboards: 1

parts:
  PUSHBUTTON = Pushbutton [package="[SMD]"]
  CL_SWITCH = SPST Switch [package=switch-spdt_kit]
  LM2907 = LM2907M [package=THT]
  Power_Lever_POT_10K = POT [package=pot_mammoth]
  10K = 10K Ω Resistor [package="1206 [SMD]"]
  10K1 = 10K Ω Resistor [package="1206 [SMD]"]
  10K_2 = 10K Ω Resistor [package="1206 [SMD]"]
  R1 = 10K Ω Resistor [package="1206 [SMD]"]
  C4 = Ceramic Capacitor [package="100 mil [THT, multilayer]"]
  0_01_uF = Ceramic Capacitor [package="100 mil [THT, multilayer]"]
  Particle_Photon = Photon

nets (from the breadboard view):
  N1: PUSHBUTTON.Pin_1, PUSHBUTTON.Pin_2, 10K_2.Pin_0, Particle_Photon.D2
  N2: PUSHBUTTON.Pin_3, PUSHBUTTON.Pin_4, CL_SWITCH.S, Particle_Photon.3V3
  N3: CL_SWITCH.O, 10K.Pin_0
  N4: CL_SWITCH.P, Particle_Photon.D4
  N5: LM2907.Serial_In, 0_01_uF.1
  N6: LM2907.In_4_/_ADC_4, LM2907.In_3_/_Infrain, R1.Pin_0, C4.1
  N7: LM2907.In_2, LM2907.Out_3, 10K1.Pin_0, Particle_Photon.A2
  N8: LM2907.Out_5, LM2907.Out_4, Power_Lever_POT_10K.E, Particle_Photon.VIN
  N9: LM2907.Out_2, LM2907.Out_1, Power_Lever_POT_10K.S, 10K.Pin_1, 10K1.Pin_1, 10K_2.Pin_1, R1.Pin_1, C4.0, 0_01_uF.0, Particle_Photon.GND
  N10: Power_Lever_POT_10K.A, Particle_Photon.A0

notes:
  To ESC TTL Control
  to Fan Motor
  3.3V Rails
  5VRails
  Speed Sense F2V Circuit

custom parts:
  LM2907M: Texas Instruments Demodulator
  10K Ω Resistor: A generic resistor
  10K Ω Resistor: A generic resistor
  Ceramic Capacitor: 100 nF multilayer Ceramic Capacitor
  Ceramic Capacitor: 100 nF multilayer Ceramic Capacitor
