# Fritzing sketch photonWind (saved by Fritzing 0.9.3b)
breadboards: 1

parts:
  PUSHBUTTON = Pushbutton [package="[SMD]"]
  CL_SWITCH = SPST Switch [package=switch-spdt_kit]
  LM2907 = LM2907M [package=THT]
  Power_Lever_POT_10K = POT [package=pot_mammoth]
  10K = 10K Ω Resistor [package="1206 [SMD]"]
  10K1 = 10K Ω Resistor [package="1206 [SMD]"]
  10K_2 = 10K Ω Resistor [package="1206 [SMD]"]
  R1 = 10K Ω Resistor [package="1206 [SMD]"]
  C4 = Ceramic Capacitor [package="100 mil [THT, multilayer]"]
  0_01_uF = Ceramic Capacitor [package="100 mil [THT, multilayer]"]
  Particle_Photon = Photon
  100 = Resistor [tolerance=±5% resistance=220 package=THT]
  100_2 = Resistor [tolerance=±5% resistance=220 package=THT]
  Particle_Photon1 = Photon
  Particle_Photon2 = Photon
  100_3 = Resistor [tolerance=±5% resistance=220 package=THT]

nets (from the breadboard view):
  N1: PUSHBUTTON.Pin_1, PUSHBUTTON.Pin_2, 10K_2.Pin_0, Particle_Photon.D2, Particle_Photon1.D2, Particle_Photon2.D2
  3V3: PUSHBUTTON.Pin_3, PUSHBUTTON.Pin_4, CL_SWITCH.S, LM2907.Out_5, LM2907.Out_4, Power_Lever_POT_10K.E, Particle_Photon.3V3, Particle_Photon1.3V3, Particle_Photon2.3V3
  N2: CL_SWITCH.O, 10K.Pin_0
  N3: CL_SWITCH.P, Particle_Photon.D4, Particle_Photon1.D4, Particle_Photon2.D4
  N4: LM2907.+V, 100.Pin_1, 100_2.Pin_0
  N5: LM2907.Serial_In, 0_01_uF.1
  N6: LM2907.In_4_/_ADC_4, LM2907.In_3_/_Infrain, R1.Pin_0, C4.1
  N7: LM2907.In_2, LM2907.Out_3, 10K1.Pin_0, Particle_Photon.A2, Particle_Photon1.A2, Particle_Photon2.A2
  GND: LM2907.Out_2, LM2907.Out_1, Power_Lever_POT_10K.S, 10K.Pin_1, 10K1.Pin_1, 10K_2.Pin_1, R1.Pin_1, C4.0, 0_01_uF.0, Particle_Photon.GND, Particle_Photon1.GND, Particle_Photon2.GND, 100_3.Pin_0
  N8: Power_Lever_POT_10K.A, Particle_Photon.A0, Particle_Photon1.A0, Particle_Photon2.A0
  N9: Particle_Photon.A1, Particle_Photon1.A1, Particle_Photon2.A1
  N10: Particle_Photon.A3, Particle_Photon1.A3, Particle_Photon2.A3
  N11: Particle_Photon.A4, Particle_Photon1.A4, Particle_Photon2.A4
  N12: Particle_Photon.A5, Particle_Photon1.A5, Particle_Photon2.A5
  N13: Particle_Photon.DAC, Particle_Photon1.DAC, Particle_Photon2.DAC
  N14: Particle_Photon.WKP, Particle_Photon1.WKP, Particle_Photon2.WKP
  N15: Particle_Photon.RX, Particle_Photon1.RX, Particle_Photon2.RX
  N16: Particle_Photon.TX, Particle_Photon1.TX, Particle_Photon2.TX
  VIN: Particle_Photon.VIN, Particle_Photon1.VIN, Particle_Photon2.VIN
  N17: Particle_Photon.D0, Particle_Photon1.D0, Particle_Photon2.D0
  N18: Particle_Photon.D1, Particle_Photon1.D1, Particle_Photon2.D1
  N19: Particle_Photon.D3, Particle_Photon1.D3, Particle_Photon2.D3
  N20: Particle_Photon.D5, Particle_Photon1.D5, Particle_Photon2.D5
  N21: Particle_Photon.D6, Particle_Photon1.D6, Particle_Photon2.D6
  N22: Particle_Photon.D7, Particle_Photon1.D7, Particle_Photon2.D7
  N23: Particle_Photon.VBAT, Particle_Photon1.VBAT, Particle_Photon2.VBAT
  N24: Particle_Photon.RST, Particle_Photon1.RST, Particle_Photon2.RST

notes:
  To ESC TTL Control
  to Fan Motor
  3.3V Rails
  5VRails
  Speed Sense F2V Circuit
  L-Attenuator

custom parts:
  LM2907M: Texas Instruments Demodulator
  10K Ω Resistor: A generic resistor
  10K Ω Resistor: A generic resistor
  Ceramic Capacitor: 100 nF multilayer Ceramic Capacitor
  Ceramic Capacitor: 100 nF multilayer Ceramic Capacitor
  Photon: The Photon is a tiny Wi-Fi development board that makes it easy to create internet-connected hardware. The Photon is all you need to get started. Power it over USB and in minutes you'll be controlling LEDs, switches, and motors and collecting data from sensors over the internet! It has 18 digital I/O pins, 8 analog input pins, 2 analog outputs (DAC), 9 PWM pins; UART (Serial), SPI, I2S, I2C,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
